// Logisim project logismCPU.circ as structural Verilog: 1 circuit, main circuit main
module main (
);

  wire and_1_out, and_2_out, and_3_out, and_4_out, and_5_out, and_6_out, and_7_out, and_8_out, and_9_out,
       and_10_out, and_11_out, and_12_out, and_13_out, and_14_out, and_15_out, and_16_out, and_17_out,
       and_18_out, and_19_out, and_20_out, and_21_out, and_22_out, and_23_out, and_24_out, and_25_out,
       and_26_out, and_27_out, button_1_out, button_2_out, button_3_out, button_4_out, clock_1_out,
       comparator_1_eq, comparator_1_gt, comparator_1_lt, controlled_buffer_19_out, counter_2_carry,
       counter_3_carry, counter_3_q, decoder_1_out0, decoder_1_out1, decoder_1_out2, decoder_1_out3,
       decoder_2_out0, decoder_2_out1, decoder_2_out2, decoder_2_out3, decoder_2_out4, decoder_2_out5,
       decoder_2_out6, decoder_2_out7, decoder_2_out8, decoder_2_out9, decoder_2_out10, decoder_2_out11,
       decoder_3_out0, decoder_3_out1, decoder_3_out2, decoder_3_out3, decoder_3_out4, decoder_3_out5,
       decoder_3_out6, decoder_3_out7, decoder_4_out0, decoder_4_out1, decoder_4_out2, decoder_5_out0,
       decoder_5_out1, decoder_5_out2, decoder_5_out3, nor_1_out, nor_2_out, or_1_out, or_2_out, or_3_out,
       or_4_out, or_5_out, or_6_out, or_7_out, or_8_out, or_9_out, or_10_out, or_11_out, or_12_out,
       or_13_out, or_14_out, or_15_out, or_16_out, or_17_out, or_18_out, or_19_out, or_20_out, or_21_out,
       or_22_out, or_23_out, or_24_out;
  wire [1:0] counter_2_q;
  wire [2:0] rom_1_data;
  wire [3:0] register_1_q;
  wire [15:0] adder_1_out, adder_2_out, bit_extender_1_out, controlled_buffer_1_out, controlled_buffer_3_out,
       controlled_buffer_4_out, controlled_buffer_7_out, controlled_buffer_10_out, controlled_buffer_13_out,
       controlled_buffer_14_out, controlled_buffer_16_out, controlled_buffer_17_out,
       controlled_buffer_18_out, counter_1_q, ram_1_dout, register_2_q, register_3_q, register_4_q,
       register_5_q, register_6_q, register_7_q, register_8_q, register_9_q, register_10_q, register_11_q,
       register_12_q;
  wire [15:3] rom_1_data_2;
  wire [15:4] register_1_q_2;

  Button button_1 (.out(button_1_out));
  Button button_2 (.out(button_2_out));
  Button button_3 (.out(button_3_out));
  Button button_4 (.out(button_4_out));
  nor nor_1 (nor_1_out, button_1_out, nor_2_out);
  or or_1 (or_1_out, nor_1_out, button_4_out, decoder_2_out0);
  nor nor_2 (nor_2_out, or_1_out, button_2_out);
  Clock clock_1 (.out(clock_1_out));
  and and_1 (and_1_out, clock_1_out, nor_2_out);
  or or_2 (or_2_out, and_1_out, button_3_out);
  or or_3 (or_3_out, button_1_out, button_4_out);
  or or_4 (or_4_out, and_2_out, or_9_out, and_4_out, or_10_out);
  and and_2 (and_2_out, and_3_out, counter_2_carry);
  and and_3 (and_3_out, or_2_out, counter_3_carry);
  Counter #(.width(16), .max('hffff), .trigger("falling")) counter_1 (
    .clr(or_3_out), .load(or_5_out), .up(1'b1), .count(1'b1), .clk(or_4_out), .D(controlled_buffer_1_out),
    .Q(counter_1_q));  // open: carry
  or or_5 (or_5_out, or_12_out, decoder_2_out8);
  Counter #(.width(2), .max('h3), .trigger("falling")) counter_2 (
    .clr(or_6_out), .load(1'b0), .up(1'b1), .count(1'b1), .clk(and_3_out), .carry(counter_2_carry),
    .Q(counter_2_q));  // open: D
  or or_6 (or_6_out, or_3_out, or_9_out, and_4_out, or_10_out);
  Counter #(.width(1), .max('h1), .trigger("falling")) counter_3 (
    .clr(or_7_out), .load(1'b0), .up(1'b1), .count(1'b1), .clk(or_2_out), .carry(counter_3_carry),
    .Q(counter_3_q));  // open: D
  or or_7 (or_7_out, or_9_out, or_3_out, and_4_out, or_10_out);
  ROM #(.addrWidth(18), .dataWidth(16)) rom_1 (.addr({counter_1_q, counter_2_q}), .data({rom_1_data_2, rom_1_data}));
  or or_8 (or_8_out, counter_2_q[1], counter_2_q[0]);
  assign controlled_buffer_1_out = decoder_2_out8 ? register_5_q : 16'bz;  // Controlled_Buffer controlled_buffer_1
  and and_4 (and_4_out, decoder_2_out8, counter_3_q);
  or or_9 (or_9_out, and_5_out, and_6_out);
  and and_5 (and_5_out, or_11_out, counter_3_q, decoder_2_out7);
  or or_10 (or_10_out, and_7_out, and_10_out);
  or or_11 (or_11_out, register_5_q[0], register_5_q[1], register_5_q[2], register_5_q[3], register_5_q[4], register_5_q[5], register_5_q[6], register_5_q[7], register_5_q[8], register_5_q[9], register_5_q[10], register_5_q[11], register_5_q[12], register_5_q[13], register_5_q[14], register_5_q[15]);
  assign controlled_buffer_1_out = or_12_out ? {rom_1_data_2, rom_1_data} : 16'bz;  // Controlled_Buffer controlled_buffer_2
  or or_12 (or_12_out, decoder_2_out7, decoder_2_out6);
  and and_6 (and_6_out, decoder_2_out6, counter_3_q);
  Decoder #(.select(2)) decoder_1 (
    .out0(decoder_1_out0), .out1(decoder_1_out1), .out2(decoder_1_out2), .out3(decoder_1_out3),
    .sel(counter_2_q));  // open: en
  and and_7 (and_7_out, decoder_1_out3, or_14_out);
  Register #(.width(16)) register_1 (
    .D({rom_1_data_2, rom_1_data}), .clk(and_8_out), .Q({register_1_q_2, register_1_q}), .clr(or_3_out));  // open: en
  and and_8 (and_8_out, decoder_1_out0, counter_3_q);
  Register #(.width(16)) register_2 (
    .D({rom_1_data_2, rom_1_data}), .clk(and_9_out), .Q(register_2_q), .clr(or_3_out));  // open: en
  and and_9 (and_9_out, decoder_1_out1, counter_3_q, or_16_out);
  Decoder #(.select(4)) decoder_2 (
    .out0(decoder_2_out0), .out1(decoder_2_out1), .out2(decoder_2_out2), .out3(decoder_2_out3),
    .out4(decoder_2_out4), .out5(decoder_2_out5), .out6(decoder_2_out6), .out7(decoder_2_out7),
    .out8(decoder_2_out8), .out9(decoder_2_out9), .out10(decoder_2_out10), .out11(decoder_2_out11),
    .sel(register_1_q), .en(or_8_out));  // open: out12, out13, out14, out15
  and and_10 (and_10_out, decoder_1_out2, or_15_out);
  or or_13 (or_13_out, and_18_out, decoder_2_out4, and_17_out);
  or or_14 (or_14_out, or_16_out, decoder_2_out5, decoder_2_out3);
  or or_15 (or_15_out, decoder_2_out7, decoder_2_out10, decoder_2_out11, decoder_2_out9);
  assign controlled_buffer_3_out = or_13_out ? register_2_q : 16'bz;  // Controlled_Buffer controlled_buffer_3
  Register #(.width(16)) register_3 (
    .D({rom_1_data_2, rom_1_data}), .clk(and_11_out), .Q(register_3_q), .clr(or_3_out));  // open: en
  and and_11 (and_11_out, decoder_2_out3, counter_3_q, decoder_1_out1);
  or or_16 (or_16_out, decoder_2_out1, decoder_2_out4, decoder_2_out2);
  assign controlled_buffer_4_out = and_12_out ? register_3_q : 16'bz;  // Controlled_Buffer controlled_buffer_4
  and and_12 (and_12_out, decoder_2_out3, decoder_1_out2);
  and and_13 (and_13_out, and_12_out, counter_3_q);
  or or_17 (or_17_out, and_13_out, and_14_out, and_16_out);
  and and_14 (and_14_out, counter_3_q, and_23_out);
  and and_15 (and_15_out, decoder_2_out10, counter_3_q);
  and and_16 (and_16_out, counter_3_q, and_18_out);
  and and_17 (and_17_out, decoder_2_out2, decoder_1_out2);
  and and_18 (and_18_out, decoder_1_out2, decoder_2_out1);
  and and_19 (and_19_out, and_17_out, counter_3_q);
  and and_20 (and_20_out, decoder_2_out4, decoder_1_out2);
  and and_21 (and_21_out, decoder_2_out5, decoder_1_out1);
  and and_22 (and_22_out, and_21_out, counter_3_q);
  and and_23 (and_23_out, decoder_2_out5, decoder_1_out2);
  and and_24 (and_24_out, decoder_2_out11, counter_3_q);
  and and_25 (and_25_out, counter_3_q, decoder_2_out9);
  or or_18 (or_18_out, and_25_out, or_17_out);
  or or_19 (or_19_out, and_26_out, decoder_2_out10, decoder_2_out11, and_17_out);
  or or_20 (or_20_out, and_18_out, decoder_2_out9);
  or or_21 (or_21_out, or_20_out, and_27_out, and_24_out, and_15_out, and_19_out);
  and and_26 (and_26_out, decoder_2_out4, decoder_1_out2);
  and and_27 (and_27_out, and_26_out, counter_3_q);
  Adder #(.width(16)) adder_1 (.a(register_4_q), .b(register_5_q), .out(adder_1_out));  // open: cin, cout
  or or_22 (or_22_out, decoder_2_out10, decoder_2_out11, decoder_2_out9);
  assign controlled_buffer_3_out = or_22_out ? adder_1_out : 16'bz;  // Controlled_Buffer controlled_buffer_5
  RAM #(.addrWidth(16), .dataWidth(16), .databus("bibus")) ram_1 (
    .addr(controlled_buffer_3_out), .we(or_19_out), .oe(or_20_out), .clk(or_21_out),
    .din(controlled_buffer_7_out), .dout(ram_1_dout));
  Register #(.width(16)) register_4 (
    .D(controlled_buffer_4_out), .clk(decoder_3_out1), .Q(register_4_q), .clr(or_3_out));  // open: en
  Register #(.width(16)) register_5 (
    .D(controlled_buffer_4_out), .clk(decoder_3_out0), .Q(register_5_q), .clr(or_3_out));  // open: en
  Register #(.width(16)) register_6 (
    .D(controlled_buffer_4_out), .clk(decoder_3_out2), .Q(register_6_q), .clr(or_3_out));  // open: en
  assign controlled_buffer_4_out = or_20_out ? ram_1_dout : 16'bz;  // Controlled_Buffer controlled_buffer_6
  assign controlled_buffer_7_out = and_20_out ? {rom_1_data_2, rom_1_data} : 16'bz;  // Controlled_Buffer controlled_buffer_7
  assign controlled_buffer_7_out = decoder_2_out11 ? register_6_q : 16'bz;  // Controlled_Buffer controlled_buffer_8
  Register #(.width(16)) register_7 (
    .D(controlled_buffer_7_out), .clk(and_22_out), .Q(register_7_q), .clr(or_3_out));  // open: en
  assign controlled_buffer_4_out = and_23_out ? register_7_q : 16'bz;  // Controlled_Buffer controlled_buffer_9
  or or_23 (or_23_out, and_21_out, decoder_2_out10, and_17_out);
  assign controlled_buffer_10_out = or_23_out ? {rom_1_data_2, rom_1_data} : 16'bz;  // Controlled_Buffer controlled_buffer_10
  Decoder #(.select(3)) decoder_3 (
    .out0(decoder_3_out0), .out1(decoder_3_out1), .out2(decoder_3_out2), .out3(decoder_3_out3),
    .out4(decoder_3_out4), .out5(decoder_3_out5), .out6(decoder_3_out6), .out7(decoder_3_out7),
    .sel(rom_1_data), .en(or_18_out));
  Decoder #(.select(3)) decoder_4 (
    .out0(decoder_4_out0), .out1(decoder_4_out1), .out2(decoder_4_out2), .sel(controlled_buffer_10_out[2:0]),
    .en(or_23_out));  // open: out3, out4, out5, out6, out7
  Register #(.width(16)) register_8 (
    .D(controlled_buffer_4_out), .clk(decoder_3_out3), .Q(register_8_q), .clr(or_3_out));  // open: en
  assign controlled_buffer_7_out = decoder_4_out1 ? adder_1_out : 16'bz;  // Controlled_Buffer controlled_buffer_11
  assign controlled_buffer_7_out = decoder_4_out0 ? register_8_q : 16'bz;  // Controlled_Buffer controlled_buffer_12
  Register #(.width(16)) register_9 (
    .D(controlled_buffer_4_out), .clk(decoder_3_out4), .Q(register_9_q), .clr(or_3_out));  // open: en
  assign controlled_buffer_13_out = decoder_5_out0 ? register_9_q : 16'bz;  // Controlled_Buffer controlled_buffer_13
  assign controlled_buffer_14_out = decoder_5_out0 ? register_10_q : 16'bz;  // Controlled_Buffer controlled_buffer_14
  assign controlled_buffer_7_out = decoder_4_out2 ? controlled_buffer_18_out : 16'bz;  // Controlled_Buffer controlled_buffer_15
  Register #(.width(16)) register_10 (
    .D(controlled_buffer_4_out), .clk(decoder_3_out5), .Q(register_10_q), .clr(or_3_out));  // open: en
  assign controlled_buffer_16_out = or_24_out ? register_9_q : 16'bz;  // Controlled_Buffer controlled_buffer_16
  or or_24 (or_24_out, decoder_5_out1, decoder_5_out2, decoder_5_out3);
  assign controlled_buffer_17_out = or_24_out ? register_10_q : 16'bz;  // Controlled_Buffer controlled_buffer_17
  Comparator #(.width(16), .mode("unsigned")) comparator_1 (
    .a(controlled_buffer_16_out), .b(controlled_buffer_17_out), .gt(comparator_1_gt), .eq(comparator_1_eq),
    .lt(comparator_1_lt));
  Adder #(.width(16)) adder_2 (
    .a(controlled_buffer_14_out), .b(controlled_buffer_13_out), .out(adder_2_out));  // open: cin, cout
  assign controlled_buffer_18_out = decoder_5_out0 ? adder_2_out : 16'bz;  // Controlled_Buffer controlled_buffer_18
  Register #(.width(16)) register_11 (
    .D(controlled_buffer_4_out), .clk(decoder_3_out6), .Q(register_11_q), .clr(or_3_out));  // open: en
  assign controlled_buffer_19_out = decoder_5_out1 ? comparator_1_gt : 1'bz;  // Controlled_Buffer controlled_buffer_19
  assign controlled_buffer_19_out = decoder_5_out2 ? comparator_1_eq : 1'bz;  // Controlled_Buffer controlled_buffer_20
  assign controlled_buffer_19_out = decoder_5_out3 ? comparator_1_lt : 1'bz;  // Controlled_Buffer controlled_buffer_21
  assign controlled_buffer_18_out = or_24_out ? bit_extender_1_out : 16'bz;  // Controlled_Buffer controlled_buffer_22
  Register #(.width(16)) register_12 (
    .D(controlled_buffer_4_out), .clk(decoder_3_out7), .Q(register_12_q), .clr(or_3_out));  // open: en
  Decoder #(.select(3)) decoder_5 (
    .out0(decoder_5_out0), .out1(decoder_5_out1), .out2(decoder_5_out2), .out3(decoder_5_out3),
    .sel(register_11_q[2:0]));  // open: out4, out5, out6, out7, en
  assign bit_extender_1_out = {{15{1'b0}}, controlled_buffer_19_out};  // Bit_Extender bit_extender_1
  Hex_Digit_Display hex_digit_display_1 (.value(register_12_q[15:12]));  // open: dp
  Hex_Digit_Display hex_digit_display_2 (.value(register_12_q[11:8]));  // open: dp
  Hex_Digit_Display hex_digit_display_3 (.value(register_12_q[7:4]));  // open: dp
  Hex_Digit_Display hex_digit_display_4 (.value(register_12_q[3:0]));  // open: dp

  // Notes on the sheet:
  //   On
  //   Off
  //   Reset
  //   One Step
  //   contents of rom_1 (hex, n*v repeats v):
  //   4 0 0 0 1 0 7 0 3 0 6 0 3 1 5 0 1 0 4 0 2 0 2 0 3 2 6 0 3 a 5 0 1 0 4 0 5 2 0 0 7 c 0 0 6 1 6*0 9 5
  //   0 0 3 0 6 0 3 5 0 0 5 2 2 0 b 0 0 0 3 5 0 0 9 2 0 0 3 2 0 0 9 0 0 0 3 0 1 0 b 0 0 0 5 0 1 0 3
endmodule
